// Logisim project mem_store_and_load.circ as structural Verilog: 1 circuit, main circuit main
module main (
  input  in_1,
  input  in_2,
  input  in_3
);

  wire and_1_out, and_2_out, and_3_out, clock_1_out, not_1_out, not_2_out, s_r_ff_1_q;

  not not_1 (not_1_out, in_2);
  not not_2 (not_2_out, in_3);
  and and_1 (and_1_out, in_1, not_1_out, not_2_out);
  Clock clock_1 (.out(clock_1_out));
  and and_2 (and_2_out, in_2, in_1, not_2_out);
  S_R_Flip_Flop s_r_ff_1 (
    .S(and_2_out), .clk(clock_1_out), .R(and_1_out), .Q(s_r_ff_1_q));  // open: Qn, preset, reset, en
  and and_3 (and_3_out, s_r_ff_1_q, in_1, in_3);
  LED led_1 (.in(and_3_out));
endmodule
