// Logisim project mem_temp.circ as structural Verilog: 5 circuits, main circuit BC
module BC (
  input  in_1,
  input  in_2,
  input  in_3,
  input  in_4,
  output out_5
);

  wire and_1_out, and_2_out, not_1_out, not_2_out, s_r_ff_1_q;

  not not_1 (not_1_out, in_2);
  not not_2 (not_2_out, in_4);
  and and_1 (and_1_out, in_1, not_1_out, not_2_out);
  and and_2 (and_2_out, in_2, in_1, not_2_out);
  S_R_Flip_Flop s_r_ff_1 (.S(and_2_out), .clk(in_3), .R(and_1_out), .Q(s_r_ff_1_q));  // open: Qn, preset, reset, en
  and and_3 (out_5, s_r_ff_1_q, in_1, in_4);
endmodule

module four_cross_four_module (
  input  I0,
  input  I1,
  input  I2,
  input  I3,
  input  E,
  input  [1:0] Addr,
  input  R_W,
  output O0,
  output O1,
  output O2,
  output O3
);

  wire bc_1_out_5, bc_2_out_5, bc_3_out_5, bc_4_out_5, bc_5_out_5, bc_6_out_5, bc_7_out_5, bc_8_out_5,
       bc_9_out_5, bc_10_out_5, bc_11_out_5, bc_12_out_5, bc_13_out_5, bc_14_out_5, bc_15_out_5, bc_16_out_5,
       clock_1_out, decoder_1_out0, decoder_1_out1, decoder_1_out2, decoder_1_out3, or_1_out, or_2_out,
       or_3_out, or_4_out;

  Decoder #(.select(2)) decoder_1 (
    .out0(decoder_1_out0), .out1(decoder_1_out1), .out2(decoder_1_out2), .out3(decoder_1_out3), .sel(Addr),
    .en(E));
  Clock clock_1 (.out(clock_1_out));
  BC bc_1 (.in_2(I0), .in_3(clock_1_out), .in_1(decoder_1_out0), .in_4(R_W), .out_5(bc_1_out_5));
  BC bc_2 (.in_2(I0), .in_3(clock_1_out), .in_1(decoder_1_out1), .in_4(R_W), .out_5(bc_2_out_5));
  BC bc_3 (.in_2(I0), .in_3(clock_1_out), .in_1(decoder_1_out2), .in_4(R_W), .out_5(bc_3_out_5));
  BC bc_4 (.in_2(I0), .in_3(clock_1_out), .in_1(decoder_1_out3), .in_4(R_W), .out_5(bc_4_out_5));
  or or_1 (or_1_out, bc_3_out_5, bc_2_out_5, bc_1_out_5, bc_4_out_5);
  BC bc_5 (.in_2(I1), .in_3(clock_1_out), .in_1(decoder_1_out0), .in_4(R_W), .out_5(bc_5_out_5));
  BC bc_6 (.in_2(I1), .in_3(clock_1_out), .in_1(decoder_1_out1), .in_4(R_W), .out_5(bc_6_out_5));
  BC bc_7 (.in_2(I1), .in_3(clock_1_out), .in_1(decoder_1_out2), .in_4(R_W), .out_5(bc_7_out_5));
  BC bc_8 (.in_2(I1), .in_3(clock_1_out), .in_1(decoder_1_out3), .in_4(R_W), .out_5(bc_8_out_5));
  or or_2 (or_2_out, bc_7_out_5, bc_6_out_5, bc_5_out_5, bc_8_out_5);
  and and_1 (O0, or_1_out, E);
  BC bc_9 (.in_2(I2), .in_3(clock_1_out), .in_1(decoder_1_out0), .in_4(R_W), .out_5(bc_9_out_5));
  BC bc_10 (.in_2(I2), .in_3(clock_1_out), .in_1(decoder_1_out1), .in_4(R_W), .out_5(bc_10_out_5));
  BC bc_11 (.in_2(I2), .in_3(clock_1_out), .in_1(decoder_1_out2), .in_4(R_W), .out_5(bc_11_out_5));
  BC bc_12 (.in_2(I2), .in_3(clock_1_out), .in_1(decoder_1_out3), .in_4(R_W), .out_5(bc_12_out_5));
  and and_2 (O1, or_2_out, E);
  BC bc_13 (.in_2(I3), .in_3(clock_1_out), .in_1(decoder_1_out0), .in_4(R_W), .out_5(bc_13_out_5));
  BC bc_14 (.in_2(I3), .in_3(clock_1_out), .in_1(decoder_1_out1), .in_4(R_W), .out_5(bc_14_out_5));
  BC bc_15 (.in_2(I3), .in_3(clock_1_out), .in_1(decoder_1_out2), .in_4(R_W), .out_5(bc_15_out_5));
  BC bc_16 (.in_2(I3), .in_3(clock_1_out), .in_1(decoder_1_out3), .in_4(R_W), .out_5(bc_16_out_5));
  or or_3 (or_3_out, bc_11_out_5, bc_10_out_5, bc_9_out_5, bc_12_out_5);
  and and_3 (O2, or_3_out, E);
  or or_4 (or_4_out, bc_16_out_5, bc_15_out_5, bc_14_out_5, bc_13_out_5);
  and and_4 (O3, or_4_out, E);
endmodule

module _32x4 (
  input  I0,
  input  I1,
  input  I2,
  input  I3,
  input  E,
  input  [4:0] Addr,
  input  R_W,
  output O0,
  output O1,
  output O2,
  output O0_2
);

  wire decoder_1_out0, decoder_1_out1, decoder_1_out2, decoder_1_out3, decoder_1_out4, decoder_1_out5,
       decoder_1_out6, decoder_1_out7, four_cross_four_module_1_o0, four_cross_four_module_1_o1,
       four_cross_four_module_1_o2, four_cross_four_module_1_o3, four_cross_four_module_2_o0,
       four_cross_four_module_2_o1, four_cross_four_module_2_o2, four_cross_four_module_2_o3,
       four_cross_four_module_3_o0, four_cross_four_module_3_o1, four_cross_four_module_3_o2,
       four_cross_four_module_3_o3, four_cross_four_module_4_o0, four_cross_four_module_4_o1,
       four_cross_four_module_4_o2, four_cross_four_module_4_o3, four_cross_four_module_5_o0,
       four_cross_four_module_5_o1, four_cross_four_module_5_o2, four_cross_four_module_5_o3,
       four_cross_four_module_6_o0, four_cross_four_module_6_o1, four_cross_four_module_6_o2,
       four_cross_four_module_6_o3, four_cross_four_module_7_o0, four_cross_four_module_7_o1,
       four_cross_four_module_7_o2, four_cross_four_module_7_o3, four_cross_four_module_8_o0,
       four_cross_four_module_8_o1, four_cross_four_module_8_o2, four_cross_four_module_8_o3, or_1_out,
       or_2_out, or_3_out, or_4_out;

  Decoder #(.select(3)) decoder_1 (
    .out0(decoder_1_out0), .out1(decoder_1_out1), .out2(decoder_1_out2), .out3(decoder_1_out3),
    .out4(decoder_1_out4), .out5(decoder_1_out5), .out6(decoder_1_out6), .out7(decoder_1_out7),
    .sel(Addr[4:2]), .en(E));
  four_cross_four_module four_cross_four_module_1 (
    .E(decoder_1_out0), .Addr(Addr[1:0]), .R_W(R_W), .I0(I0), .I1(I1), .I2(I2), .I3(I3),
    .O0(four_cross_four_module_1_o0), .O1(four_cross_four_module_1_o1), .O2(four_cross_four_module_1_o2),
    .O3(four_cross_four_module_1_o3));
  four_cross_four_module four_cross_four_module_2 (
    .E(decoder_1_out1), .Addr(Addr[1:0]), .R_W(R_W), .I0(I0), .I1(I1), .I2(I2), .I3(I3),
    .O0(four_cross_four_module_2_o0), .O1(four_cross_four_module_2_o1), .O2(four_cross_four_module_2_o2),
    .O3(four_cross_four_module_2_o3));
  four_cross_four_module four_cross_four_module_3 (
    .E(decoder_1_out2), .Addr(Addr[1:0]), .R_W(R_W), .I0(I0), .I1(I1), .I2(I2), .I3(I3),
    .O0(four_cross_four_module_3_o0), .O1(four_cross_four_module_3_o1), .O2(four_cross_four_module_3_o2),
    .O3(four_cross_four_module_3_o3));
  four_cross_four_module four_cross_four_module_4 (
    .E(decoder_1_out3), .Addr(Addr[1:0]), .R_W(R_W), .I0(I0), .I1(I1), .I2(I2), .I3(I3),
    .O0(four_cross_four_module_4_o0), .O1(four_cross_four_module_4_o1), .O2(four_cross_four_module_4_o2),
    .O3(four_cross_four_module_4_o3));
  four_cross_four_module four_cross_four_module_5 (
    .E(decoder_1_out4), .Addr(Addr[1:0]), .R_W(R_W), .I0(I0), .I1(I1), .I2(I2), .I3(I3),
    .O0(four_cross_four_module_5_o0), .O1(four_cross_four_module_5_o1), .O2(four_cross_four_module_5_o2),
    .O3(four_cross_four_module_5_o3));
  four_cross_four_module four_cross_four_module_6 (
    .E(decoder_1_out5), .Addr(Addr[1:0]), .R_W(R_W), .I0(I0), .I1(I1), .I2(I2), .I3(I3),
    .O0(four_cross_four_module_6_o0), .O1(four_cross_four_module_6_o1), .O2(four_cross_four_module_6_o2),
    .O3(four_cross_four_module_6_o3));
  four_cross_four_module four_cross_four_module_7 (
    .E(decoder_1_out6), .Addr(Addr[1:0]), .R_W(R_W), .I0(I0), .I1(I1), .I2(I2), .I3(I3),
    .O0(four_cross_four_module_7_o0), .O1(four_cross_four_module_7_o1), .O2(four_cross_four_module_7_o2),
    .O3(four_cross_four_module_7_o3));
  four_cross_four_module four_cross_four_module_8 (
    .E(decoder_1_out7), .Addr(Addr[1:0]), .R_W(R_W), .I0(I0), .I1(I1), .I2(I2), .I3(I3),
    .O0(four_cross_four_module_8_o0), .O1(four_cross_four_module_8_o1), .O2(four_cross_four_module_8_o2),
    .O3(four_cross_four_module_8_o3));
  or or_1 (or_1_out, four_cross_four_module_1_o0, four_cross_four_module_2_o0, four_cross_four_module_3_o0, four_cross_four_module_4_o0, four_cross_four_module_5_o0, four_cross_four_module_6_o0, four_cross_four_module_7_o0, four_cross_four_module_8_o0);
  or or_2 (or_2_out, four_cross_four_module_1_o1, four_cross_four_module_2_o1, four_cross_four_module_3_o1, four_cross_four_module_4_o1, four_cross_four_module_5_o1, four_cross_four_module_6_o1, four_cross_four_module_7_o1, four_cross_four_module_8_o1);
  or or_3 (or_3_out, four_cross_four_module_1_o2, four_cross_four_module_2_o2, four_cross_four_module_3_o2, four_cross_four_module_4_o2, four_cross_four_module_5_o2, four_cross_four_module_6_o2, four_cross_four_module_7_o2, four_cross_four_module_8_o2);
  or or_4 (or_4_out, four_cross_four_module_1_o3, four_cross_four_module_2_o3, four_cross_four_module_3_o3, four_cross_four_module_4_o3, four_cross_four_module_5_o3, four_cross_four_module_6_o3, four_cross_four_module_7_o3, four_cross_four_module_8_o3);
  and and_1 (O0, or_1_out, E);
  and and_2 (O1, or_2_out, E);
  and and_3 (O2, or_3_out, E);
  and and_4 (O0_2, or_4_out, E);
endmodule

module TEMP (
  input  in_1,
  input  in_2,
  input  in_3,
  input  in_4,
  input  in_5,
  input  in_6
);

  wire n256x4_1_o0, n256x4_1_o0_2, n256x4_1_o1, n256x4_1_o2, undriven_2;
  wire [7:1] undriven;

  _256X4 u_256x4_1 (
    .Addr({undriven, in_5}), .E(undriven_2), .R_W(in_6), .I0(in_1), .I1(in_2), .I2(in_3), .I3(in_4),
    .O0(n256x4_1_o0), .O1(n256x4_1_o1), .O2(n256x4_1_o2), .O0_2(n256x4_1_o0_2));
  LED led_1 (.in(n256x4_1_o0));
  _256X4 u_256x4_2 ();  // open: Addr, E, R_W, I0, I1, I2, I3, O0, O1, O2, O0_2
  LED led_2 (.in(n256x4_1_o0_2));
  LED led_3 (.in(n256x4_1_o2));
  LED led_4 (.in(n256x4_1_o1));
  // Pins of 1 and 8 bits meet at {undriven, in_5}
endmodule

module _256X4 (
  input  I0,
  input  I1,
  input  I2,
  input  I3,
  input  [7:0] Addr,
  input  E,
  input  R_W,
  output O0,
  output O1,
  output O2,
  output O0_2
);

  wire decoder_1_out0, decoder_1_out1, decoder_1_out2, decoder_1_out3, decoder_1_out4, decoder_1_out5,
       decoder_1_out6, decoder_1_out7, n32x4_1_o0, n32x4_1_o0_2, n32x4_1_o1, n32x4_1_o2, n32x4_2_o0,
       n32x4_2_o0_2, n32x4_2_o1, n32x4_2_o2, n32x4_3_o0, n32x4_3_o0_2, n32x4_3_o1, n32x4_3_o2, n32x4_4_o0,
       n32x4_4_o0_2, n32x4_4_o1, n32x4_4_o2, n32x4_5_o0, n32x4_5_o0_2, n32x4_5_o1, n32x4_5_o2, n32x4_6_o0,
       n32x4_6_o0_2, n32x4_6_o1, n32x4_6_o2, n32x4_7_o0, n32x4_7_o0_2, n32x4_7_o1, n32x4_7_o2, n32x4_8_o0,
       n32x4_8_o0_2, n32x4_8_o1, n32x4_8_o2, or_1_out, or_2_out, or_3_out, or_4_out;

  Decoder #(.select(3)) decoder_1 (
    .out0(decoder_1_out0), .out1(decoder_1_out1), .out2(decoder_1_out2), .out3(decoder_1_out3),
    .out4(decoder_1_out4), .out5(decoder_1_out5), .out6(decoder_1_out6), .out7(decoder_1_out7),
    .sel(Addr[7:5]), .en(E));
  _32x4 u_32x4_1 (
    .E(decoder_1_out0), .Addr(Addr[4:0]), .R_W(R_W), .I0(I0), .I1(I1), .I2(I2), .I3(I3), .O0(n32x4_1_o0),
    .O1(n32x4_1_o1), .O2(n32x4_1_o2), .O0_2(n32x4_1_o0_2));
  _32x4 u_32x4_2 (
    .E(decoder_1_out1), .Addr(Addr[4:0]), .R_W(R_W), .I0(I0), .I1(I1), .I2(I2), .I3(I3), .O0(n32x4_2_o0),
    .O1(n32x4_2_o1), .O2(n32x4_2_o2), .O0_2(n32x4_2_o0_2));
  _32x4 u_32x4_3 (
    .E(decoder_1_out2), .Addr(Addr[4:0]), .R_W(R_W), .I0(I0), .I1(I1), .I2(I2), .I3(I3), .O0(n32x4_3_o0),
    .O1(n32x4_3_o1), .O2(n32x4_3_o2), .O0_2(n32x4_3_o0_2));
  _32x4 u_32x4_4 (
    .E(decoder_1_out3), .Addr(Addr[4:0]), .R_W(R_W), .I0(I0), .I1(I1), .I2(I2), .I3(I3), .O0(n32x4_4_o0),
    .O1(n32x4_4_o1), .O2(n32x4_4_o2), .O0_2(n32x4_4_o0_2));
  _32x4 u_32x4_5 (
    .E(decoder_1_out4), .Addr(Addr[4:0]), .R_W(R_W), .I0(I0), .I1(I1), .I2(I2), .I3(I3), .O0(n32x4_5_o0),
    .O1(n32x4_5_o1), .O2(n32x4_5_o2), .O0_2(n32x4_5_o0_2));
  _32x4 u_32x4_6 (
    .E(decoder_1_out5), .Addr(Addr[4:0]), .R_W(R_W), .I0(I0), .I1(I1), .I2(I2), .I3(I3), .O0(n32x4_6_o0),
    .O1(n32x4_6_o1), .O2(n32x4_6_o2), .O0_2(n32x4_6_o0_2));
  _32x4 u_32x4_7 (
    .E(decoder_1_out6), .Addr(Addr[4:0]), .R_W(R_W), .I0(I0), .I1(I1), .I2(I2), .I3(I3), .O0(n32x4_7_o0),
    .O1(n32x4_7_o1), .O2(n32x4_7_o2), .O0_2(n32x4_7_o0_2));
  _32x4 u_32x4_8 (
    .E(decoder_1_out7), .Addr(Addr[4:0]), .R_W(R_W), .I0(I0), .I1(I1), .I2(I2), .I3(I3), .O0(n32x4_8_o0),
    .O1(n32x4_8_o1), .O2(n32x4_8_o2), .O0_2(n32x4_8_o0_2));
  or or_1 (or_1_out, n32x4_1_o0, n32x4_2_o0, n32x4_3_o0, n32x4_4_o0, n32x4_5_o0, n32x4_6_o0, n32x4_7_o0, n32x4_8_o0);
  or or_2 (or_2_out, n32x4_1_o1, n32x4_2_o1, n32x4_3_o1, n32x4_4_o1, n32x4_5_o1, n32x4_6_o1, n32x4_7_o1, n32x4_8_o1);
  or or_3 (or_3_out, n32x4_1_o2, n32x4_2_o2, n32x4_3_o2, n32x4_4_o2, n32x4_5_o2, n32x4_6_o2, n32x4_7_o2, n32x4_8_o2);
  or or_4 (or_4_out, n32x4_1_o0_2, n32x4_2_o0_2, n32x4_3_o0_2, n32x4_4_o0_2, n32x4_5_o0_2, n32x4_6_o0_2, n32x4_7_o0_2, n32x4_8_o0_2);
  and and_1 (O0, or_1_out, E);
  and and_2 (O1, or_2_out, E);
  and and_3 (O2, or_3_out, E);
  and and_4 (O0_2, or_4_out, E);
endmodule
